# Fritzing sketch BLDC_ESC (saved by Fritzing 0.9.4)

parts:
  Part1 = Arduino Uno (Rev3)
  920KV_Motor1 = DJI 920 KV Motor
  M1 = ESC
  12_V = Power plug  # not connected
  R1 = Rotary Potentiometer (Large) [maximum_resistance=100kΩ package=THT]

nets:
  N1: Part1.A0, R1.wiper
  N2: Part1.D9_PWM, M1.DATA
  N3: Part1.5V, R1.leg2
  GND: Part1.GND, M1.GND, R1.leg1
  N4: 920KV_Motor1.w, M1.W
  N5: 920KV_Motor1.v, M1.V
  N6: 920KV_Motor1.u, M1.U

notes:
  ADAPTER

custom parts:
  DJI 920 KV Motor: DJI Brushless Outrunner 2212/920K Motor F330-550
