# Fritzing sketch BipolarStepper (saved by Fritzing 0.9.4)
breadboards: 1

parts:
  DRV_1 = DRV 8825 Stepper Motor Carrier, High Current [part_number="DRV 8825"]
  Part1 = Arduino Uno (Rev3) - ICSP
  12_V_DC = Power plug
  47_u = Capacitor Polarized [package=panasonic_c]  # not connected
  M1 = Stepper Motor - Bipolar

nets:
  N1: DRV_1.RESET, DRV_1.SLEEP, Part1.5V
  N2: DRV_1.STEP, Part1.D9_PWM
  N3: DRV_1.DIRECTION, Part1.D8
  N4: DRV_1.VOLTAGE_ST/_MT, 12_V_DC.VCC
  GND: DRV_1.GROUND_ST/_MT, DRV_1.GROUND_LOG, Part1.GND, 12_V_DC.GND
  N5: DRV_1.OUT_2B, M1.A
  N6: DRV_1.OUT_2A, M1.C
  N7: DRV_1.OUT_1A, M1.B
  N8: DRV_1.OUT_1B, M1.D
