# Fritzing sketch L298N-TT-DC-Motor (saved by Fritzing 0.9.6b)

parts:
  M1 = DC Motor
  M2 = DC Motor
  L298N1 = L298N DC motor driver
  Raspberry_Pi_1 = Raspberry Pi 3 [part_number=RPI-3-V1.2]
  7_4_V_DC = Power plug

nets (from the breadboard view):
  N1: M1.pin_1, L298N1.OUT2
  N2: M1.pin_2, L298N1.OUT1
  N3: M2.pin_1, L298N1.OUT3
  N4: M2.pin_2, L298N1.OUT4
  12V: L298N1.12V, 7_4_V_DC.VCC
  GND: L298N1.GND, Raspberry_Pi_1.GND, 7_4_V_DC.GND
  N5: L298N1.ENA, Raspberry_Pi_1.GPIO6
  N6: L298N1.ENB, Raspberry_Pi_1.GPIO12
  N7: L298N1.IN1, Raspberry_Pi_1.GPIO26
  N8: L298N1.IN2, Raspberry_Pi_1.GPIO19
  N9: L298N1.IN3, Raspberry_Pi_1.GPIO20
  N10: L298N1.IN4, Raspberry_Pi_1.GPIO16

custom parts:
  L298N DC motor driver: 2x DC motor driver with 78M05 positive voltage regulator (7..35 V) L298N: max 46 V, 2 A Set 5 V Enable jumper to enable 5 V regultor (needed for the L298N) and +5 V output at screw terminal or supply external +5 V at screw terminal Set ENA and/or ENB to +5 V to enable motor permanently or supply ENA and/or ENB with PWM signal IN1 and IN2 set rotation directory for motor A (OUT1/OUT2) IN2 and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
