# Fritzing sketch Pi_Pico_Stepper (saved by Fritzing 0.9.6b)
breadboards: 1

parts:
  Mod1 = Raspberry Pi Pico
  Driver1 = 28BYJ-48 Driver Module [part_number=ULN2003 package=THT]
  part = 28BYJ-48 Stepper Motor [part_number=28BYJ-48]
  5_VDC = Power plug

nets:
  GND: Mod1.pin_3, Mod1.pin_8, Mod1.pin_13, Mod1.pin_18, Mod1.pin_23, Mod1.pin_28, Mod1.pin_33, Mod1.pin_38, Mod1.pin_42, Driver1.GND, 5_VDC.GND
  N1: Mod1.pin_4, Driver1.IN1
  N2: Mod1.pin_5, Driver1.IN2
  N3: Mod1.pin_6, Driver1.IN3
  N4: Mod1.pin_7, Driver1.IN4
  N5: Driver1.Vmotor, 5_VDC.VCC
  N6: Driver1.blue-pin, part.blue-pin
  N7: Driver1.pink-pin, part.pink-pin
  N8: Driver1.yellow-pin, part.yellow-pin
  N9: Driver1.orange-pin, part.orange-pin
  N10: Driver1.red-pin, part.red-pin

custom parts:
  Raspberry Pi Pico: Raspberry Pi Pico. Based around the RP2040 microcontroller the Pico is a low cost microcontroller device bringing Raspberry Pi quality, cost, and easy of use to the microcontroller space. Jan 2021, Split part in to two versions: tht (this one) and SMD. This one will drill holes for a .1 in header in pcb to allow plugging in the module as well as providing pads to solder the module to the top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
  28BYJ-48 Driver Module: ULN2003 Driver Module for the 28BYJ-48 Unipolar Stepper Motor LED A - Blue wire - Bottom coil left LED B - Pink wire - Top coil left LED C - Yellow wire - Bottom coil right LED D - Orange wire - Top coil right Common rail - red Connector pins: blue - pink - yellow - orange - red Control pins - IN1 to IN4 Power pins - GND & Vmotor (5-12V) On/Off jumper (if removed, power to motor is cut).
  28BYJ-48 Stepper Motor: Unipolar Stepper Motor 28BYJ-48 Top coil - pink & orange Bottom coil - blue & yellow Common rail - red Connector pins: blue - pink - yellow - orange - red
