# Fritzing sketch ServoRaspberry (saved by Fritzing 0.9.4)

parts:
  Servo_Tilt = Basic Servo
  Raspberry_Pi_1 = Raspberry Pi 3 [part_number=RPI-3-V1.2]
  Servo_Pan = Basic Servo
  5_V = Power plug

nets:
  GND: Servo_Tilt.gnd, Raspberry_Pi_1.GND, Servo_Pan.gnd, 5_V.GND
  VCC: Servo_Tilt.vcc, Servo_Pan.vcc, 5_V.VCC
  N1: Servo_Tilt.pulse, Raspberry_Pi_1.GPIO17
  N2: Raspberry_Pi_1.GPIO18, Servo_Pan.pulse
